// Logisim project LCD.circ as structural Verilog: 1 circuit, main circuit main
module main (
  input  x4,
  input  x3,
  input  x2,
  input  x1
);

  wire nand_1_out, nand_2_out, nand_3_out, nand_4_out, nand_5_out, nand_6_out, nand_7_out, nand_8_out,
       nand_9_out, nand_10_out, nand_11_out, nand_12_out, nand_13_out, nand_14_out, nand_15_out, nand_16_out,
       nand_17_out, not_1_out, not_2_out, not_3_out, not_4_out, not_5_out;

  not not_1 (not_1_out, x4);
  not not_2 (not_2_out, x3);
  not not_3 (not_3_out, x2);
  not not_4 (not_4_out, x1);
  nand nand_1 (nand_1_out, x1, x3);
  nand nand_2 (nand_2_out, not_4_out, not_2_out);
  nand nand_3 (nand_3_out, not_4_out, not_3_out);
  nand nand_4 (nand_4_out, x1, x2);
  nand nand_5 (nand_5_out, not_4_out, x2, not_2_out);
  nand nand_6 (nand_6_out, not_3_out, x3);
  nand nand_7 (nand_7_out, x2, not_2_out);
  nand nand_8 (nand_8_out, x1, not_3_out, x3);
  nand nand_9 (nand_9_out, not_4_out, not_3_out);
  nand nand_10 (nand_10_out, not_3_out, not_1_out, nand_1_out, nand_2_out);
  nand nand_11 (nand_11_out, x3, nand_3_out, nand_4_out);
  nand nand_12 (nand_12_out, not_4_out, nand_6_out);
  nand nand_13 (nand_13_out, nand_6_out, not_4_out);
  nand nand_14 (nand_14_out, not_2_out, not_1_out, nand_9_out);
  nand nand_15 (nand_15_out, nand_1_out, x2);
  nand nand_16 (nand_16_out, not_1_out, nand_12_out, nand_7_out, nand_8_out);
  not not_5 (not_5_out, nand_13_out);
  nand nand_17 (nand_17_out, nand_6_out, nand_15_out, not_1_out);
  _7_Segment_Display u_7_segment_display_1 (
    .g(nand_17_out), .f(nand_14_out), .a(nand_10_out), .b(nand_11_out), .e(not_5_out), .d(nand_16_out),
    .c(nand_5_out));  // open: dp
endmodule
