// Logisim project Sterownik_LCD.circ as structural Verilog: 1 circuit, main circuit main
module main (
  input  in_1,
  input  in_2,
  input  in_3,
  input  in_4
);

  wire [7:0] rom_1_data;

  ROM #(.addrWidth(4)) rom_1 (.addr({in_1, in_2, in_3, in_4}), .data(rom_1_data));  // open: sel
  _7_Segment_Display u_7_segment_display_1 (
    .g(rom_1_data[7]), .f(rom_1_data[6]), .a(rom_1_data[5]), .b(rom_1_data[4]), .e(rom_1_data[3]),
    .d(rom_1_data[2]), .c(rom_1_data[1]), .dp(rom_1_data[0]));

  // Notes on the sheet:
  //   contents of rom_1 (hex, n*v repeats v):
  //   7e 12 bc b6 d2 e6 ee 72 fe f6 6*80
endmodule
