// Logisim project Frequency_Counter.circ as structural Verilog: 1 circuit, main circuit main
module main (
  output f_2,
  output f_4,
  output f_8,
  output f_16
);

  wire clock_1_out, d_ff_1_qn, d_ff_2_qn, d_ff_3_qn, d_ff_4_qn;

  Clock clock_1 (.out(clock_1_out));
  D_Flip_Flop #(.trigger("falling")) d_ff_1 (
    .clk(clock_1_out), .D(d_ff_1_qn), .Q(f_2), .Qn(d_ff_1_qn));  // open: preset, en, reset
  D_Flip_Flop #(.trigger("falling")) d_ff_2 (
    .clk(f_2), .D(d_ff_2_qn), .Q(f_4), .Qn(d_ff_2_qn));  // open: preset, en, reset
  D_Flip_Flop #(.trigger("falling")) d_ff_3 (
    .clk(f_4), .D(d_ff_3_qn), .Q(f_8), .Qn(d_ff_3_qn));  // open: preset, en, reset
  D_Flip_Flop #(.trigger("falling")) d_ff_4 (
    .clk(f_8), .D(d_ff_4_qn), .Q(f_16), .Qn(d_ff_4_qn));  // open: preset, en, reset

  // Notes on the sheet:
  //   f
  //   Dzielnik częstotliwości
endmodule
