// Logisim project Komparator.circ as structural Verilog: 1 circuit, main circuit main
module main (
  input  A,
  input  B,
  output A_B,
  output A__B,
  output A_B_2,
  output out_6,
  output out_7,
  output out_8
);

  wire and_3_out, and_4_out;

  Comparator #(.width(1)) comparator_1 (.a(A), .b(B), .gt(out_6), .eq(out_7), .lt(out_8));
  and and_1 (A_B, A, ~B);  // AND_Gate
  and and_2 (A_B_2, ~A, B);  // AND_Gate
  and and_3 (and_3_out, A, B);
  and and_4 (and_4_out, ~A, ~B);  // AND_Gate
  or or_1 (A__B, and_3_out, and_4_out);

  // Notes on the sheet:
  //   KOMPARATOR 1 BITOWY WŁASNY I GOTOWY
endmodule
