// Logisim project SUM_SUBSTR.circ as structural Verilog: 6 circuits, main circuit main
module main (
  input  a3,
  input  a3_2,
  input  a2,
  input  a2_2,
  input  a1,
  input  a1_2,
  input  a0,
  input  a0_2,
  input  b3,
  input  b3_2,
  input  b2,
  input  b2_2,
  input  b1,
  input  b1_2,
  input  b0,
  input  b0_2
);

  wire SEG_A_2_out_5, SEG_A_2_out_6, SEG_A_2_out_7, SEG_A_2_out_8, SEG_A_2_out_9, SEG_A_2_out_10,
       SEG_A_2_out_11, SEG_A_2_out_12, SEG_A_out_5, SEG_A_out_6, SEG_A_out_7, SEG_A_out_8, SEG_A_out_9,
       SEG_A_out_10, SEG_A_out_11, SEG_A_out_12, SEG_B_2_out_5, SEG_B_2_out_6, SEG_B_2_out_7, SEG_B_2_out_8,
       SEG_B_2_out_9, SEG_B_2_out_10, SEG_B_2_out_11, SEG_B_2_out_12, SEG_B_out_5, SEG_B_out_6, SEG_B_out_7,
       SEG_B_out_8, SEG_B_out_9, SEG_B_out_10, SEG_B_out_11, SEG_B_out_12, SEG_S_2_out_5, SEG_S_2_out_6,
       SEG_S_2_out_7, SEG_S_2_out_8, SEG_S_2_out_9, SEG_S_2_out_10, SEG_S_2_out_11, SEG_S_2_out_12,
       SEG_S_out_5, SEG_S_out_6, SEG_S_out_7, SEG_S_out_8, SEG_S_out_9, SEG_S_out_10, SEG_S_out_11,
       SEG_S_out_12, SUB_s0, SUB_s1, SUB_s2, SUB_s3, SUM_s0, SUM_s1, SUM_s2, SUM_s3;

  _4Bit_SUM SUM (
    .a3(a3), .a2(a2), .a1(a1), .a0(a0), .b3(b3), .b2(b2), .b1(b1), .b0(b0), .S3(SUM_s3), .S2(SUM_s2),
    .S1(SUM_s1), .S0(SUM_s0));  // open: C
  _7Seg SEG_A (
    .x3(a3), .x2(a2), .x1(a1), .x0(a0), .out_5(SEG_A_out_5), .out_6(SEG_A_out_6), .out_7(SEG_A_out_7),
    .out_8(SEG_A_out_8), .out_9(SEG_A_out_9), .out_10(SEG_A_out_10), .out_11(SEG_A_out_11),
    .out_12(SEG_A_out_12));
  _7Seg SEG_B (
    .x3(b3), .x2(b2), .x1(b1), .x0(b0), .out_5(SEG_B_out_5), .out_6(SEG_B_out_6), .out_7(SEG_B_out_7),
    .out_8(SEG_B_out_8), .out_9(SEG_B_out_9), .out_10(SEG_B_out_10), .out_11(SEG_B_out_11),
    .out_12(SEG_B_out_12));
  _7_Segment_Display u_7_segment_display_1 (
    .g(SEG_A_out_8), .f(SEG_A_out_7), .a(SEG_A_out_6), .b(SEG_A_out_5), .e(SEG_A_out_9), .d(SEG_A_out_10),
    .c(SEG_A_out_11), .dp(SEG_A_out_12));
  _7_Segment_Display u_7_segment_display_2 (
    .g(SEG_B_out_8), .f(SEG_B_out_7), .a(SEG_B_out_6), .b(SEG_B_out_5), .e(SEG_B_out_9), .d(SEG_B_out_10),
    .c(SEG_B_out_11), .dp(SEG_B_out_12));
  _7Seg SEG_S (
    .x3(SUM_s3), .x2(SUM_s2), .x1(SUM_s1), .x0(SUM_s0), .out_5(SEG_S_out_5), .out_6(SEG_S_out_6),
    .out_7(SEG_S_out_7), .out_8(SEG_S_out_8), .out_9(SEG_S_out_9), .out_10(SEG_S_out_10),
    .out_11(SEG_S_out_11), .out_12(SEG_S_out_12));
  _7_Segment_Display u_7_segment_display_3 (
    .g(SEG_S_out_8), .f(SEG_S_out_7), .a(SEG_S_out_6), .b(SEG_S_out_5), .e(SEG_S_out_9), .d(SEG_S_out_10),
    .c(SEG_S_out_11), .dp(SEG_S_out_12));
  _4Bit__SUB SUB (
    .a3(a3_2), .a2(a2_2), .a1(a1_2), .a0(a0_2), .b3(b3_2), .b2(b2_2), .b1(b1_2), .b0(b0_2), .S3(SUB_s3),
    .S2(SUB_s2), .S1(SUB_s1), .S0(SUB_s0));  // open: C
  _7Seg SEG_A_2 (
    .x3(a3_2), .x2(a2_2), .x1(a1_2), .x0(a0_2), .out_5(SEG_A_2_out_5), .out_6(SEG_A_2_out_6),
    .out_7(SEG_A_2_out_7), .out_8(SEG_A_2_out_8), .out_9(SEG_A_2_out_9), .out_10(SEG_A_2_out_10),
    .out_11(SEG_A_2_out_11), .out_12(SEG_A_2_out_12));
  _7_Segment_Display u_7_segment_display_4 (
    .g(SEG_A_2_out_8), .f(SEG_A_2_out_7), .a(SEG_A_2_out_6), .b(SEG_A_2_out_5), .e(SEG_A_2_out_9),
    .d(SEG_A_2_out_10), .c(SEG_A_2_out_11), .dp(SEG_A_2_out_12));
  _7Seg SEG_B_2 (
    .x3(b3_2), .x2(b2_2), .x1(b1_2), .x0(b0_2), .out_5(SEG_B_2_out_5), .out_6(SEG_B_2_out_6),
    .out_7(SEG_B_2_out_7), .out_8(SEG_B_2_out_8), .out_9(SEG_B_2_out_9), .out_10(SEG_B_2_out_10),
    .out_11(SEG_B_2_out_11), .out_12(SEG_B_2_out_12));
  _7_Segment_Display u_7_segment_display_5 (
    .g(SEG_B_2_out_8), .f(SEG_B_2_out_7), .a(SEG_B_2_out_6), .b(SEG_B_2_out_5), .e(SEG_B_2_out_9),
    .d(SEG_B_2_out_10), .c(SEG_B_2_out_11), .dp(SEG_B_2_out_12));
  _7Seg SEG_S_2 (
    .x3(SUB_s3), .x2(SUB_s2), .x1(SUB_s1), .x0(SUB_s0), .out_5(SEG_S_2_out_5), .out_6(SEG_S_2_out_6),
    .out_7(SEG_S_2_out_7), .out_8(SEG_S_2_out_8), .out_9(SEG_S_2_out_9), .out_10(SEG_S_2_out_10),
    .out_11(SEG_S_2_out_11), .out_12(SEG_S_2_out_12));
  _7_Segment_Display u_7_segment_display_6 (
    .g(SEG_S_2_out_8), .f(SEG_S_2_out_7), .a(SEG_S_2_out_6), .b(SEG_S_2_out_5), .e(SEG_S_2_out_9),
    .d(SEG_S_2_out_10), .c(SEG_S_2_out_11), .dp(SEG_S_2_out_12));

  // Notes on the sheet:
  //   DODAWANIE
  //   ODEJMOWANIE
endmodule

module _7Seg (
  input  x3,
  input  x2,
  input  x1,
  input  x0,
  output out_5,
  output out_6,
  output out_7,
  output out_8,
  output out_9,
  output out_10,
  output out_11,
  output out_12
);

  ROM #(.addrWidth(4)) rom_1 (
    .addr({x3, x2, x1, x0}), .data({out_12, out_6, out_5, out_11, out_10, out_9, out_7, out_8}));  // open: sel

  // Notes on the sheet:
  //   x0: pull=down
  //   x2: pull=down
  //   x1: pull=down
  //   x3: pull=down
  //   contents of rom_1 (hex, n*v repeats v):
  //   7e 30 6d 79 33 5b 5f 70 7f 7b
endmodule

module SUM (
  input  A,
  input  B,
  input  C__i_1,
  output S,
  output C
);

  wire and_1_out, and_2_out, xor_1_out;

  xor xor_1 (xor_1_out, A, B);
  xor xor_2 (S, xor_1_out, C__i_1);
  and and_1 (and_1_out, A, B);
  and and_2 (and_2_out, xor_1_out, C__i_1);
  or or_1 (C, and_1_out, and_2_out);

  // Notes on the sheet:
  //   S
endmodule

module _4Bit_SUM (
  input  a3,
  input  a2,
  input  a1,
  input  a0,
  input  b3,
  input  b2,
  input  b1,
  input  b0,
  output S3,
  output S2,
  output S1,
  output S0,
  output C
);

  wire SUM0_c, SUM1_c, SUM2_c;

  SUM SUM0 (.A(a0), .B(b0), .C__i_1(1'b0), .S(S0), .C(SUM0_c));
  SUM SUM1 (.A(a1), .B(b1), .C__i_1(SUM0_c), .S(S1), .C(SUM1_c));
  SUM SUM2 (.A(a2), .B(b2), .C__i_1(SUM1_c), .S(S2), .C(SUM2_c));
  SUM SUM3 (.A(a3), .B(b3), .C__i_1(SUM2_c), .S(S3), .C(C));
endmodule

module SUB (
  input  A,
  input  B,
  input  C__i_1,
  output S,
  output C
);

  wire and_1_out, and_2_out, not_1_out, xor_1_out, xor_3_out;

  xor xor_1 (xor_1_out, A, B);
  not not_1 (not_1_out, A);
  xor xor_2 (S, xor_1_out, C__i_1);
  and and_1 (and_1_out, not_1_out, B);
  xor xor_3 (xor_3_out, not_1_out, B);
  and and_2 (and_2_out, xor_3_out, C__i_1);
  or or_1 (C, and_1_out, and_2_out);

  // Notes on the sheet:
  //   S
endmodule

module _4Bit__SUB (
  input  a3,
  input  a2,
  input  a1,
  input  a0,
  input  b3,
  input  b2,
  input  b1,
  input  b0,
  output S3,
  output S2,
  output S1,
  output S0,
  output C
);

  wire SUB0_c, SUB2_c, SUM1_c;

  SUB SUB0 (.A(a0), .B(b0), .C__i_1(1'b0), .S(S0), .C(SUB0_c));
  SUB SUM1 (.A(a1), .B(b1), .C__i_1(SUB0_c), .S(S1), .C(SUM1_c));
  SUB SUB2 (.A(a2), .B(b2), .C__i_1(SUM1_c), .S(S2), .C(SUB2_c));
  SUB SUM3 (.A(a3), .B(b3), .C__i_1(SUB2_c), .S(S3), .C(C));
endmodule
