// Logisim project Sumator_1b.circ as structural Verilog: 1 circuit, main circuit main
module main (
  input  A,
  input  B,
  input  C_i,
  output Y,
  output C_0
);

  wire and_1_out, and_2_out, and_3_out, and_4_out, and_5_out, and_6_out, and_7_out, and_8_out, and_9_out,
       or_1_out, or_2_out;

  and and_1 (and_1_out, ~A, ~B);  // AND_Gate
  and and_2 (and_2_out, A, B);
  and and_3 (and_3_out, ~A, B);  // AND_Gate
  and and_4 (and_4_out, ~B, A);  // AND_Gate
  or or_1 (or_1_out, and_1_out, and_2_out);
  or or_2 (or_2_out, and_3_out, and_4_out);
  and and_5 (and_5_out, A, B);
  and and_6 (and_6_out, B, C_i);
  and and_7 (and_7_out, A, C_i);
  and and_8 (and_8_out, C_i, or_1_out);
  and and_9 (and_9_out, ~C_i, or_2_out);  // AND_Gate
  or or_3 (C_0, and_5_out, and_6_out, and_7_out);
  or or_4 (Y, and_8_out, and_9_out);

  // Notes on the sheet:
  //   Sumator jednobitowy
endmodule
