// Logisim project DeMorgan.circ as structural Verilog: 1 circuit, main circuit main
module main (
  input  in_1,
  input  in_2,
  output out_3,
  output out_4
);

  wire not_1_out, not_2_out;

  not not_1 (not_1_out, in_1);
  not not_2 (not_2_out, in_2);
  nand nand_1 (out_3, in_1, in_2);
  or or_1 (out_4, not_1_out, not_2_out);
endmodule
