// Logisim project Y1_PKD.circ as structural Verilog: 1 circuit, main circuit main
module main (
  input  a,
  input  b,
  input  c,
  output out_4
);

  wire and_1_out, and_2_out, and_3_out, and_4_out, and_5_out;

  and and_1 (and_1_out, ~a, ~b, ~c);  // AND_Gate
  and and_2 (and_2_out, ~a, ~b, c);  // AND_Gate
  and and_3 (and_3_out, ~a, b, ~c);  // AND_Gate
  and and_4 (and_4_out, ~a, b, c);  // AND_Gate
  and and_5 (and_5_out, a, ~b, c);  // AND_Gate
  or or_1 (out_4, and_1_out, and_2_out, and_3_out, and_4_out, and_5_out);

  // Notes on the sheet:
  //   Postać kanoniczna dysjunkcyjna
endmodule
