// Logisim project Y3.circ as structural Verilog: 1 circuit, main circuit main
module main (
  input  in_1,
  input  in_2,
  input  in_3,
  output out_4,
  output out_5
);

  wire and_1_out, and_2_out, and_3_out, or_1_out, or_2_out, or_3_out, or_4_out, or_5_out;

  and and_1 (and_1_out, ~in_1, in_2, ~in_3);  // AND_Gate
  and and_2 (and_2_out, in_1, ~in_2, ~in_3);  // AND_Gate
  and and_3 (and_3_out, in_1, in_2, in_3);
  or or_1 (or_1_out, in_1, in_2, in_3);
  or or_2 (or_2_out, in_1, in_2, ~in_3);  // OR_Gate
  or or_3 (or_3_out, in_1, ~in_2, ~in_3);  // OR_Gate
  or or_4 (or_4_out, ~in_1, in_2, ~in_3);  // OR_Gate
  or or_5 (or_5_out, ~in_1, ~in_2, in_3);  // OR_Gate
  or or_6 (out_4, and_1_out, and_2_out, and_3_out);
  and and_4 (out_5, or_1_out, or_2_out, or_3_out, or_4_out, or_5_out);
endmodule
