// Logisim project Y5-PND-NAND.circ as structural Verilog: 1 circuit, main circuit main
module main (
  input  a,
  input  b,
  input  c,
  output PKD,
  output PKK,
  output PND,
  output PND_____NAND
);

  wire and_1_out, and_2_out, and_3_out, and_4_out, and_5_out, and_6_out, nand_1_out, nand_2_out, not_1_out,
       not_2_out, not_3_out, or_1_out, or_2_out, or_3_out;

  not not_1 (not_1_out, a);
  not not_2 (not_2_out, b);
  not not_3 (not_3_out, c);
  and and_1 (and_1_out, not_1_out, not_2_out, not_3_out);
  and and_2 (and_2_out, not_1_out, not_2_out, c);
  and and_3 (and_3_out, not_1_out, b, not_3_out);
  and and_4 (and_4_out, not_1_out, b, c);
  and and_5 (and_5_out, a, not_2_out, c);
  or or_1 (or_1_out, not_1_out, b, c);
  or or_2 (or_2_out, not_1_out, not_2_out, c);
  or or_3 (or_3_out, not_1_out, not_2_out, not_3_out);
  and and_6 (and_6_out, not_2_out, c);
  nand nand_1 (nand_1_out, not_1_out, not_1_out);
  nand nand_2 (nand_2_out, not_2_out, c);
  or or_4 (PND, not_1_out, and_6_out);
  nand nand_3 (PND_____NAND, nand_1_out, nand_2_out);
  and and_7 (PKK, or_1_out, or_2_out, or_3_out);
  or or_5 (PKD, and_1_out, and_2_out, and_3_out, and_4_out, and_5_out);

  // Notes on the sheet:
  //   a'
  //   b'
  //   c
  //   a'
  //   b'
  //   c
  //   POSTAĆ KANONICZNA DYSJUNKCYJNA
  //   POSTAĆ KANONICZNA KONIUNKCYJNA
  //   POSTAĆ NORMALNA DYSJUNKCYJNA
  //   PRZEJŚCIE Z POSTACI DYSJUNKCYJNEJ (AND-OR --> NAND)
  //   a
  //   y3
  //   y4
  //   y1
  //   y2
endmodule
