// Logisim project 6b_synch_counter.circ as structural Verilog: 1 circuit, main circuit main
module main (
  output QA,
  output QB,
  output QC,
  output QD,
  output QE,
  output QF
);

  wire and_1_out, and_2_out, and_3_out, and_4_out, clock_1_out;

  Clock clock_1 (.out(clock_1_out));
  J_K_Flip_Flop #(.trigger("falling")) j_k_ff_1 (
    .J(1'b1), .clk(clock_1_out), .K(1'b1), .Q(QA));  // open: Qn, preset, en, reset
  and and_1 (and_1_out, QA, QB);
  J_K_Flip_Flop #(.trigger("falling")) j_k_ff_2 (
    .J(QA), .clk(clock_1_out), .K(QA), .Q(QB));  // open: Qn, preset, en, reset
  J_K_Flip_Flop #(.trigger("falling")) j_k_ff_3 (
    .J(and_1_out), .clk(clock_1_out), .K(and_1_out), .Q(QC));  // open: Qn, preset, en, reset
  and and_2 (and_2_out, QA, QB, QC);
  J_K_Flip_Flop #(.trigger("falling")) j_k_ff_4 (
    .J(and_2_out), .clk(clock_1_out), .K(and_2_out), .Q(QD));  // open: Qn, preset, en, reset
  and and_3 (and_3_out, QA, QB, QC, QD);
  J_K_Flip_Flop #(.trigger("falling")) j_k_ff_5 (
    .J(and_3_out), .clk(clock_1_out), .K(and_3_out), .Q(QE));  // open: Qn, preset, en, reset
  and and_4 (and_4_out, QA, QB, QC, QD, QE);
  J_K_Flip_Flop #(.trigger("falling")) j_k_ff_6 (
    .J(and_4_out), .clk(clock_1_out), .K(and_4_out), .Q(QF));  // open: Qn, preset, en, reset

  // Notes on the sheet:
  //   CLK
  //   LICZNIK SYNCHRONICZNY- 6 bitowy
endmodule
