// Logisim project CTD.circ as structural Verilog: 4 circuits, main circuit main
module main (
);

  wire and_1_out, clock_1_out, d_ff_1_q, d_ff_2_q, d_ff_2_qn, d_ff_3_q, d_ff_3_qn, d_ff_4_q, d_ff_4_qn,
       d_ff_5_q, d_ff_5_qn, not_1_out, SEG_S_out_5, SEG_S_out_6, SEG_S_out_7, SEG_S_out_8, SEG_S_out_9,
       SEG_S_out_10, SEG_S_out_11, SEG_S_out_12;

  Clock clock_1 (.out(clock_1_out));
  not not_1 (not_1_out, clock_1_out);
  D_Flip_Flop d_ff_1 (.clk(not_1_out), .D(and_1_out), .Q(d_ff_1_q));  // open: Qn, preset, en, reset
  D_Flip_Flop d_ff_2 (
    .clk(clock_1_out), .D(d_ff_2_qn), .Q(d_ff_2_q), .Qn(d_ff_2_qn), .preset(d_ff_1_q));  // open: en, reset
  D_Flip_Flop d_ff_3 (
    .clk(d_ff_2_q), .D(d_ff_3_qn), .Q(d_ff_3_q), .Qn(d_ff_3_qn), .reset(d_ff_1_q));  // open: preset, en
  D_Flip_Flop d_ff_4 (
    .clk(d_ff_3_q), .D(d_ff_4_qn), .Q(d_ff_4_q), .Qn(d_ff_4_qn), .reset(d_ff_1_q));  // open: preset, en
  D_Flip_Flop d_ff_5 (
    .clk(d_ff_4_q), .D(d_ff_5_qn), .Q(d_ff_5_q), .Qn(d_ff_5_qn), .preset(d_ff_1_q));  // open: en, reset
  and and_1 (and_1_out, d_ff_5_q, d_ff_4_q, d_ff_3_q, d_ff_2_q);
  _7Seg SEG_S (
    .x3(d_ff_5_q), .x2(d_ff_4_q), .x1(d_ff_3_q), .x0(d_ff_2_q), .out_5(SEG_S_out_5), .out_6(SEG_S_out_6),
    .out_7(SEG_S_out_7), .out_8(SEG_S_out_8), .out_9(SEG_S_out_9), .out_10(SEG_S_out_10),
    .out_11(SEG_S_out_11), .out_12(SEG_S_out_12));
  _7_Segment_Display u_7_segment_display_1 (
    .g(SEG_S_out_8), .f(SEG_S_out_7), .a(SEG_S_out_6), .b(SEG_S_out_5), .e(SEG_S_out_9), .d(SEG_S_out_10),
    .c(SEG_S_out_11), .dp(SEG_S_out_12));
endmodule

module _7Seg (
  input  x3,
  input  x2,
  input  x1,
  input  x0,
  output out_5,
  output out_6,
  output out_7,
  output out_8,
  output out_9,
  output out_10,
  output out_11,
  output out_12
);

  ROM #(.addrWidth(4)) rom_1 (
    .addr({x3, x2, x1, x0}), .data({out_12, out_6, out_5, out_11, out_10, out_9, out_7, out_8}));  // open: sel

  // Notes on the sheet:
  //   x1: pull=down
  //   x3: pull=down
  //   x0: pull=down
  //   x2: pull=down
  //   contents of rom_1 (hex, n*v repeats v):
  //   7e 30 6d 79 33 5b 5f 70 7f 7b
endmodule

module SUM (
  input  A,
  input  B,
  input  C__i_1,
  output S,
  output C
);

  wire and_1_out, and_2_out, not_1_out, xor_1_out, xor_3_out;

  xor xor_1 (xor_1_out, A, B);
  not not_1 (not_1_out, A);
  xor xor_2 (S, xor_1_out, C__i_1);
  and and_1 (and_1_out, not_1_out, B);
  xor xor_3 (xor_3_out, not_1_out, B);
  and and_2 (and_2_out, xor_3_out, C__i_1);
  or or_1 (C, and_1_out, and_2_out);

  // Notes on the sheet:
  //   S
endmodule

module _4Bit_SUM (
  input  a3,
  input  a2,
  input  a1,
  input  a0,
  input  b3,
  input  b2,
  input  b1,
  input  b0,
  output S3,
  output S2,
  output S1,
  output S0,
  output C
);

  wire SUB0_c, SUB2_c, SUM1_c;

  SUM SUB0 (.A(a0), .B(b0), .C__i_1(1'b0), .S(S0), .C(SUB0_c));
  SUM SUM1 (.A(a1), .B(b1), .C__i_1(SUB0_c), .S(S1), .C(SUM1_c));
  SUM SUB2 (.A(a2), .B(b2), .C__i_1(SUM1_c), .S(S2), .C(SUB2_c));
  SUM SUM3 (.A(a3), .B(b3), .C__i_1(SUB2_c), .S(S3), .C(C));
endmodule
