// Logisim project Liczniki_asynchroniczne.circ as structural Verilog: 1 circuit, main circuit main
module main (
  output QA,
  output QB,
  output QC,
  output QD,
  output QA_2,
  output QB_2,
  output QC_2,
  output QD_2,
  output QA_3,
  output out_10,
  output QC_3,
  output QD_3
);

  wire clock_1_out, clock_2_out, clock_3_out, d_ff_1_q, d_ff_1_qn, d_ff_2_qn, d_ff_3_qn, d_ff_4_qn,
       d_ff_5_qn, d_ff_6_q, d_ff_6_qn, d_ff_7_qn, d_ff_8_q, d_ff_8_qn, d_ff_9_qn, d_ff_10_q, d_ff_10_qn,
       d_ff_11_qn, d_ff_12_qn;

  Clock clock_1 (.out(clock_1_out));
  Clock clock_2 (.out(clock_2_out));
  Clock clock_3 (.out(clock_3_out));
  D_Flip_Flop #(.trigger("falling")) d_ff_1 (
    .clk(clock_3_out), .D(d_ff_1_qn), .Q(d_ff_1_q), .Qn(d_ff_1_qn));  // open: preset, en, reset
  D_Flip_Flop #(.trigger("falling")) d_ff_2 (
    .clk(clock_1_out), .D(d_ff_2_qn), .Q(QA), .Qn(d_ff_2_qn));  // open: preset, en, reset
  D_Flip_Flop d_ff_3 (.clk(clock_2_out), .D(d_ff_3_qn), .Q(QA_2), .Qn(d_ff_3_qn));  // open: preset, en, reset
  not not_1 (QA_3, d_ff_1_q);
  D_Flip_Flop #(.trigger("falling")) d_ff_4 (
    .clk(QA), .D(d_ff_4_qn), .Q(QB), .Qn(d_ff_4_qn));  // open: preset, en, reset
  D_Flip_Flop d_ff_5 (.clk(QA_2), .D(d_ff_5_qn), .Q(QB_2), .Qn(d_ff_5_qn));  // open: preset, en, reset
  D_Flip_Flop #(.trigger("falling")) d_ff_6 (
    .clk(d_ff_1_q), .D(d_ff_6_qn), .Q(d_ff_6_q), .Qn(d_ff_6_qn));  // open: preset, en, reset
  not not_2 (out_10, d_ff_6_q);
  D_Flip_Flop d_ff_7 (.clk(QB_2), .D(d_ff_7_qn), .Q(QC_2), .Qn(d_ff_7_qn));  // open: preset, en, reset
  D_Flip_Flop #(.trigger("falling")) d_ff_8 (
    .clk(d_ff_6_q), .D(d_ff_8_qn), .Q(d_ff_8_q), .Qn(d_ff_8_qn));  // open: preset, en, reset
  not not_3 (QC_3, d_ff_8_q);
  D_Flip_Flop #(.trigger("falling")) d_ff_9 (
    .clk(QB), .D(d_ff_9_qn), .Q(QC), .Qn(d_ff_9_qn));  // open: preset, en, reset
  D_Flip_Flop #(.trigger("falling")) d_ff_10 (
    .clk(d_ff_8_q), .D(d_ff_10_qn), .Q(d_ff_10_q), .Qn(d_ff_10_qn));  // open: preset, en, reset
  D_Flip_Flop #(.trigger("falling")) d_ff_11 (
    .clk(QC), .D(d_ff_11_qn), .Q(QD), .Qn(d_ff_11_qn));  // open: preset, en, reset
  D_Flip_Flop d_ff_12 (.clk(QC_2), .D(d_ff_12_qn), .Q(QD_2), .Qn(d_ff_12_qn));  // open: preset, en, reset
  not not_4 (QD_3, d_ff_10_q);

  // Notes on the sheet:
  //   CLK
  //   CLK
  //   CLK
  //   QB
  //   Asynchroniczny licznik szeregowy- licznik dwójkowy, bo zbocze gasnące
  //   Asynchroniczny licznik szeregowy wstecz- licznik dwójkowy, bo zbocze narastające
  //   Asynchroniczny licznik szeregowy wstecz- licznik dwójkowy, bo zbocze gasnące, ale negacja
endmodule
