// Logisim project UP_DOWN.circ as structural Verilog: 1 circuit, main circuit main
module main (
  input  _0_DOWN
);

  wire and_1_out, and_2_out, and_3_out, and_4_out, and_5_out, and_6_out, clock_1_out, j_k_ff_1_qn,
       j_k_ff_2_qn, j_k_ff_3_qn, not_1_out, or_1_out, or_2_out, or_3_out;
  wire [3:0] j_k_ff_1_q;
  wire [7:0] rom_1_data;

  Clock clock_1 (.out(clock_1_out));
  J_K_Flip_Flop j_k_ff_1 (
    .J(1'b1), .clk(clock_1_out), .K(1'b1), .Q(j_k_ff_1_q[0]), .Qn(j_k_ff_1_qn));  // open: preset, en, reset
  not not_1 (not_1_out, _0_DOWN);
  and and_1 (and_1_out, _0_DOWN, j_k_ff_1_q[0]);
  and and_2 (and_2_out, j_k_ff_1_qn, not_1_out);
  or or_1 (or_1_out, and_1_out, and_2_out);
  J_K_Flip_Flop j_k_ff_2 (
    .J(or_1_out), .clk(clock_1_out), .K(or_1_out), .Q(j_k_ff_1_q[1]), .Qn(j_k_ff_2_qn));  // open: preset, en, reset
  and and_3 (and_3_out, and_1_out, j_k_ff_1_q[1]);
  and and_4 (and_4_out, j_k_ff_2_qn, and_2_out);
  or or_2 (or_2_out, and_3_out, and_4_out);
  ROM #(.addrWidth(4)) rom_1 (.addr(j_k_ff_1_q), .data(rom_1_data));  // open: sel
  J_K_Flip_Flop j_k_ff_3 (
    .J(or_2_out), .clk(clock_1_out), .K(or_2_out), .Q(j_k_ff_1_q[2]), .Qn(j_k_ff_3_qn));  // open: preset, en, reset
  and and_5 (and_5_out, and_3_out, j_k_ff_1_q[2]);
  or or_3 (or_3_out, and_5_out, and_6_out);
  and and_6 (and_6_out, j_k_ff_3_qn, and_4_out);
  J_K_Flip_Flop j_k_ff_4 (
    .J(or_3_out), .clk(clock_1_out), .K(or_3_out), .Q(j_k_ff_1_q[3]));  // open: Qn, preset, en, reset
  _7_Segment_Display u_7_segment_display_1 (
    .g(rom_1_data[7]), .f(rom_1_data[6]), .a(rom_1_data[5]), .b(rom_1_data[4]), .e(rom_1_data[3]),
    .d(rom_1_data[2]), .c(rom_1_data[1]), .dp(rom_1_data[0]));

  // Notes on the sheet:
  //   1-UP
  //   contents of rom_1 (hex, n*v repeats v):
  //   7e 12 bc b6 d2 e6 ee 72 fe f6 6*80
endmodule
