// Logisim project D_T_JK.circ as structural Verilog: 1 circuit, main circuit main
module main (
  input  D,
  input  in_2,
  input  in_3,
  input  in_4,
  output Q,
  output out_6,
  output nQ,
  output out_8,
  output out_9,
  output out_10
);

  wire clock_1_out, clock_2_out, clock_3_out, d_ff_1_q, d_ff_3_qn, nand_1_out, nand_2_out, not_1_out;

  Clock clock_1 (.out(clock_1_out));
  Clock clock_2 (.out(clock_2_out));
  nand nand_1 (nand_1_out, D, clock_1_out);
  nand nand_2 (nand_2_out, nand_1_out, clock_1_out);
  D_Flip_Flop d_ff_1 (.clk(clock_2_out), .D(in_4), .Q(d_ff_1_q));  // open: Qn, preset, en, reset
  not not_1 (not_1_out, clock_2_out);
  D_Flip_Flop d_ff_2 (.clk(not_1_out), .D(d_ff_1_q), .Q(out_8), .Qn(out_9));  // open: preset, en, reset
  nand nand_3 (Q, nand_1_out, nQ);
  nand nand_4 (nQ, Q, nand_2_out);
  Clock clock_3 (.out(clock_3_out));
  D_Flip_Flop d_ff_3 (.clk(clock_3_out), .D(d_ff_3_qn), .Q(out_10), .Qn(d_ff_3_qn));  // open: preset, en, reset
  J_K_Flip_Flop j_k_ff_1 (.J(in_2), .clk(clock_3_out), .K(in_3), .Q(out_6));  // open: Qn, preset, en, reset

  // Notes on the sheet:
  //   C
  //   Przerzutnik D
  //   D Latch Master-Slave
endmodule
