// Logisim project SR_SRC.circ as structural Verilog: 1 circuit, main circuit main
module main (
  input  S,
  input  R,
  input  nS,
  input  nR,
  input  S_2,
  input  R_2,
  input  in_7,
  input  in_8,
  output Q,
  output Q_2,
  output Q_3,
  output nQ,
  output nQ_2,
  output nQ_3,
  output out_15,
  output out_16
);

  wire clock_1_out, clock_2_out, nand_3_out, nand_4_out;

  nor nor_1 (Q, R, nQ);
  nor nor_2 (nQ, Q, S_2);
  Clock clock_1 (.out(clock_1_out));
  S_R_Flip_Flop s_r_ff_1 (.S(in_7), .clk(clock_1_out), .R(in_8), .Q(out_15), .Qn(out_16));  // open: preset, reset, en
  nand nand_1 (Q_2, nS, nQ_2);
  nand nand_2 (nQ_2, nR, Q_2);
  Clock clock_2 (.out(clock_2_out));
  nand nand_3 (nand_3_out, S, clock_2_out);
  nand nand_4 (nand_4_out, clock_2_out, R_2);
  nand nand_5 (Q_3, nand_3_out, nQ_3);
  nand nand_6 (nQ_3, Q_3, nand_4_out);

  // Notes on the sheet:
  //   SR
  //   SR
  //   C
  //   SCR
endmodule
