// Logisim project DEMUX2.circ as structural Verilog: 1 circuit, main circuit main
module main (
  input  d,
  input  s,
  output y0,
  output y1,
  output out_5,
  output out_6
);

  Demultiplexer demultiplexer_1 (.out0(out_5), .out1(out_6), .in(d), .sel(s));  // open: en
  and and_1 (y0, ~s, d);  // AND_Gate
  and and_2 (y1, d, s);

  // Notes on the sheet:
  //   Demultiplekser zbudowany z bramek i gotowy blok
endmodule
