// Logisim project MUX2.circ as structural Verilog: 1 circuit, main circuit main
module main (
  input  A,
  input  B,
  input  S,
  output Y,
  output out_5
);

  wire and_1_out, and_2_out;

  Multiplexer multiplexer_1 (.in0(A), .in1(B), .out(out_5), .sel(S));  // open: en
  and and_1 (and_1_out, A, ~S);  // AND_Gate
  and and_2 (and_2_out, B, S);
  or or_1 (Y, and_1_out, and_2_out);

  // Notes on the sheet:
  //   Multiplekser dwuwejściowy- budowa z bramek, dla 0 przepisuje stan A dla 1 przepisuje stan B
  //   Z wykorzystaniem gotowego bloku
endmodule
