// Logisim project MUX4.circ as structural Verilog: 1 circuit, main circuit main
module main (
  input  a,
  input  b,
  input  c,
  input  d,
  input  s1,
  input  s2,
  output y
);

  wire and_1_out, and_2_out, and_3_out, and_4_out, not_1_out, not_2_out, not_3_out, not_4_out;

  not not_1 (not_1_out, s2);
  not not_2 (not_2_out, s1);
  not not_3 (not_3_out, s1);
  not not_4 (not_4_out, s2);
  and and_1 (and_1_out, d, s1, s2);
  and and_2 (and_2_out, c, s1, not_1_out);
  and and_3 (and_3_out, b, not_2_out, s2);
  and and_4 (and_4_out, a, not_3_out, not_4_out);
  or or_1 (y, and_1_out, and_2_out, and_3_out, and_4_out);
endmodule
