// Logisim project Bolean_function_with_memory.circ as structural Verilog: 1 circuit, main circuit main
module main (
  input  in_1,
  input  in_2,
  input  in_3,
  input  in_4,
  output out_5,
  output out_6
);

  wire and_1_out, and_2_out, and_3_out, and_4_out, not_1_out, not_2_out, not_3_out, not_4_out, not_5_out,
       not_6_out;
  wire [7:0] rom_1_data;

  not not_1 (not_1_out, in_1);
  not not_2 (not_2_out, in_4);
  not not_3 (not_3_out, in_3);
  not not_4 (not_4_out, in_4);
  not not_5 (not_5_out, in_2);
  not not_6 (not_6_out, in_3);
  and and_1 (and_1_out, not_1_out, not_2_out);
  and and_2 (and_2_out, not_3_out, not_4_out);
  and and_3 (and_3_out, in_2, in_3);
  and and_4 (and_4_out, in_1, not_5_out, not_6_out);
  ROM #(.addrWidth(3)) rom_1 (.addr({in_1, in_2, in_3}), .data(rom_1_data));  // open: sel
  or or_1 (out_6, and_1_out, and_2_out, and_3_out, and_4_out);
  Multiplexer multiplexer_1 (.in0(rom_1_data[0]), .in1(rom_1_data[1]), .out(out_5), .sel(in_4));  // open: en

  // Notes on the sheet:
  //   Y3
  //   contents of rom_1 (hex, n*v repeats v):
  //   1 1 1 3 3 0 1 3
endmodule
