// Logisim project Register_and_Memory.circ as structural Verilog: 1 circuit, main circuit main
module main (
  input  A,
  input  B,
  input  C,
  input  D,
  input  E,
  input  A0,
  input  A1,
  input  W,
  input  A_2,
  input  B_2,
  input  C_2,
  input  D_2,
  output QA,
  output QB,
  output QC,
  output QD,
  output QE,
  output QA_2,
  output QB_2,
  output QC_2,
  output QD_2
);

  wire and_1_out, and_2_out, and_3_out, and_4_out, and_5_out, and_6_out, and_7_out, and_8_out, and_9_out,
       and_10_out, and_11_out, and_12_out, and_13_out, and_14_out, and_15_out, and_16_out, and_17_out,
       and_18_out, and_19_out, and_20_out, and_21_out, and_22_out, and_23_out, and_24_out, clock_1_out,
       d_ff_4_q, d_ff_5_q, d_ff_6_q, d_ff_7_q, d_ff_8_q, d_ff_9_q, d_ff_10_q, d_ff_11_q, d_ff_13_q,
       d_ff_14_q, d_ff_15_q, d_ff_16_q, d_ff_18_q, d_ff_19_q, d_ff_20_q, d_ff_21_q;

  Clock clock_1 (.out(clock_1_out));
  and and_1 (and_1_out, ~A0, ~A1);  // AND_Gate
  and and_2 (and_2_out, A0, ~A1);  // AND_Gate
  and and_3 (and_3_out, ~A0, A1);  // AND_Gate
  and and_4 (and_4_out, A1, A0);
  D_Flip_Flop d_ff_1 (.clk(clock_1_out), .D(A), .Q(QA));  // open: Qn, preset, en, reset
  and and_5 (and_5_out, and_1_out, W);
  and and_6 (and_6_out, and_2_out, W);
  and and_7 (and_7_out, and_3_out, W);
  and and_8 (and_8_out, and_4_out, W);
  D_Flip_Flop d_ff_2 (.clk(clock_1_out), .D(B), .Q(QB));  // open: Qn, preset, en, reset
  D_Flip_Flop d_ff_3 (.clk(clock_1_out), .D(C), .Q(QC));  // open: Qn, preset, en, reset
  D_Flip_Flop d_ff_4 (.clk(and_5_out), .D(A_2), .Q(d_ff_4_q));  // open: Qn, preset, en, reset
  D_Flip_Flop d_ff_5 (.clk(and_6_out), .D(A_2), .Q(d_ff_5_q));  // open: Qn, preset, en, reset
  D_Flip_Flop d_ff_6 (.clk(and_7_out), .D(A_2), .Q(d_ff_6_q));  // open: Qn, preset, en, reset
  D_Flip_Flop d_ff_7 (.clk(and_8_out), .D(A_2), .Q(d_ff_7_q));  // open: Qn, preset, en, reset
  D_Flip_Flop d_ff_8 (.clk(and_5_out), .D(B_2), .Q(d_ff_8_q));  // open: Qn, preset, en, reset
  D_Flip_Flop d_ff_9 (.clk(and_6_out), .D(B_2), .Q(d_ff_9_q));  // open: Qn, preset, en, reset
  D_Flip_Flop d_ff_10 (.clk(and_7_out), .D(B_2), .Q(d_ff_10_q));  // open: Qn, preset, en, reset
  D_Flip_Flop d_ff_11 (.clk(and_8_out), .D(B_2), .Q(d_ff_11_q));  // open: Qn, preset, en, reset
  D_Flip_Flop d_ff_12 (.clk(clock_1_out), .D(D), .Q(QD));  // open: Qn, preset, en, reset
  D_Flip_Flop d_ff_13 (.clk(and_5_out), .D(C_2), .Q(d_ff_13_q));  // open: Qn, preset, en, reset
  D_Flip_Flop d_ff_14 (.clk(and_6_out), .D(C_2), .Q(d_ff_14_q));  // open: Qn, preset, en, reset
  D_Flip_Flop d_ff_15 (.clk(and_7_out), .D(C_2), .Q(d_ff_15_q));  // open: Qn, preset, en, reset
  D_Flip_Flop d_ff_16 (.clk(and_8_out), .D(C_2), .Q(d_ff_16_q));  // open: Qn, preset, en, reset
  D_Flip_Flop d_ff_17 (.D(E), .Q(QE));  // open: clk, Qn, preset, en, reset
  D_Flip_Flop d_ff_18 (.clk(and_5_out), .D(D_2), .Q(d_ff_18_q));  // open: Qn, preset, en, reset
  D_Flip_Flop d_ff_19 (.clk(and_6_out), .D(D_2), .Q(d_ff_19_q));  // open: Qn, preset, en, reset
  D_Flip_Flop d_ff_20 (.clk(and_7_out), .D(D_2), .Q(d_ff_20_q));  // open: Qn, preset, en, reset
  D_Flip_Flop d_ff_21 (.clk(and_8_out), .D(D_2), .Q(d_ff_21_q));  // open: Qn, preset, en, reset
  and and_9 (and_9_out, d_ff_4_q, and_1_out);
  and and_10 (and_10_out, d_ff_5_q, and_2_out);
  and and_11 (and_11_out, d_ff_6_q, and_3_out);
  and and_12 (and_12_out, d_ff_7_q, W);
  and and_13 (and_13_out, d_ff_8_q, and_1_out);
  and and_14 (and_14_out, d_ff_9_q, and_2_out);
  and and_15 (and_15_out, d_ff_10_q, and_3_out);
  and and_16 (and_16_out, d_ff_11_q, W);
  and and_17 (and_17_out, d_ff_13_q, and_1_out);
  and and_18 (and_18_out, d_ff_14_q, and_2_out);
  and and_19 (and_19_out, d_ff_15_q, and_3_out);
  and and_20 (and_20_out, d_ff_16_q, W);
  and and_21 (and_21_out, d_ff_18_q, and_1_out);
  and and_22 (and_22_out, d_ff_19_q, and_2_out);
  and and_23 (and_23_out, d_ff_20_q, and_3_out);
  and and_24 (and_24_out, d_ff_21_q, W);
  or or_1 (QA_2, and_9_out, and_10_out, and_11_out, and_12_out);
  or or_2 (QB_2, and_13_out, and_14_out, and_15_out, and_16_out);
  or or_3 (QC_2, and_17_out, and_18_out, and_19_out, and_20_out);
  or or_4 (QD_2, and_21_out, and_22_out, and_23_out, and_24_out);

  // Notes on the sheet:
  //   CLK
  //   dekoder adresu
  //   Pamieć rejestrowa
  //   https://eduinf.waw.pl/inf/prg/009_kurs_avr/2012.php
  //   Rejestr służy do zapamiętywania informacji bitowej oraz do przetwarzania zapamiętanej informacji
  //   rejestr
  //   Demultiplekser, który odczytuje informację z rejestru
endmodule
