// Logisim project NBC_na_1_z_8.circ as structural Verilog: 1 circuit, main circuit main
module main (
  input  d4,
  input  d2,
  input  d1,
  output _0,
  output _1,
  output _2,
  output _3,
  output _4,
  output _5,
  output _6,
  output _7
);

  and and_1 (_0, ~d4, ~d2, ~d1);  // AND_Gate
  and and_2 (_1, ~d4, ~d2, d1);  // AND_Gate
  and and_3 (_2, ~d4, d2, ~d1);  // AND_Gate
  and and_4 (_3, ~d4, d2, d1);  // AND_Gate
  and and_5 (_4, d4, ~d2, ~d1);  // AND_Gate
  and and_6 (_5, d4, ~d2, d1);  // AND_Gate
  and and_7 (_6, d4, d2, ~d1);  // AND_Gate
  and and_8 (_7, d4, d2, d1);

  // Notes on the sheet:
  //   KODER NBC 421 NA KOD 1 Z 8
endmodule
